# Fritzing sketch tone (saved by Fritzing 0.9.3b)
circuit board: 7.99008cm x 5.47772cm
breadboards: 1

parts:
  C1 = Ceramic Capacitor [capacitance=220nF package="100 mil [THT, multilayer]"]
  R1 = Trimmer Potentiometer [maximum_resistance=10kΩ package=THT]
  LED1 = LED - 5mm [color="Red (633nm)" package="5 mm [THT]"]
  R2 = Resistor [tolerance=±5% resistance=510 package=THT]
  C2 = Ceramic Capacitor [capacitance=220nF package="100 mil [THT, multilayer]"]
  D1 = Rectifier Diode [part_number=1N4148 package="300 mil [THT]"]
  C3 = Ceramic Capacitor [capacitance=2.2µF package="100 mil [THT, multilayer]"]
  C4 = Ceramic Capacitor [capacitance=220nF package="100 mil [THT, multilayer]"]
  R3 = Resistor [tolerance=±5% resistance=1k package=THT]
  R4 = Trimmer Potentiometer [maximum_resistance=5kΩ package=THT]
  Q1 = NPN-Transistor [package="TO92 [THT]"]
  R8 = Resistor [tolerance=±5% resistance=68k package=THT]
  R7 = Resistor [tolerance=±5% resistance=2.7k package=THT]
  R5 = Resistor [tolerance=±5% resistance=510 package=THT]
  LED2 = LED - 5mm [color="Red (633nm)" package="5 mm [THT]"]
  U1 = 3.5mm Audio Jack [package=audio-jack]
  U2 = 3.5mm Audio Jack [package=audio-jack]
  C5 = Ceramic Capacitor [capacitance=1µF package="100 mil [THT, multilayer]"]
  IC1 = LM567 [chip_label=IC package="DIP (Dual Inline) [THT]"]
  C6 = Ceramic Capacitor [capacitance=1nF package="100 mil [THT, multilayer]"]
  R6 = Trimmer Potentiometer [maximum_resistance=10kΩ package=THT]
  WeMos_D1_Mini1 = WeMos D1 Mini
  D2 = Rectifier Diode [part_number=1N4148 package="300 mil [THT]"]

nets:
  N1: C1.0, R1.wiper, R1.leg2, IC1.TC
  GND: C1.1, C2.1, D1.cathode, C3.1, R4.leg2, Q1.E, LED2.cathode, U2.SLEEVE, IC1.GND, C6.0, R6.leg1, WeMos_D1_Mini1.G, D2.anode
  N2: R1.leg1, IC1.TR
  N3: LED1.cathode, IC1.Out, WeMos_D1_Mini1.D2
  N4: LED1.anode, R2.Pin_1
  N5: R2.Pin_0, WeMos_D1_Mini1.3V3
  N6: C2.0, IC1.LF
  N7: D1.anode, R3.Pin_1, R4.wiper, D2.cathode
  N8: C3.0, IC1.OF
  N9: C4.0, IC1.IN
  N10: C4.1, R3.Pin_0
  N11: R4.leg1, U2.RIGHT, U2.LEFT
  N12: Q1.B, R7.Pin_1
  N13: Q1.C, U1.SLEEVE
  N14: R8.Pin_0, C6.1, R6.leg2
  N15: R8.Pin_1, WeMos_D1_Mini1.D6
  N16: R7.Pin_0, R5.Pin_0, WeMos_D1_Mini1.D7
  N17: R5.Pin_1, LED2.anode
  N18: U1.RIGHT, U1.LEFT, C5.0
  N19: C5.1, R6.wiper
  5V: IC1.V+, WeMos_D1_Mini1.5V

notes:
  Audio in
  Audio out+PTT
  Output level tuning
  Input level tuning
  Frequncy detection tuning
  (Tone detected)
  (PTT)
  Audio out
  Input
  level
  Output
  Frequency
  Detect
  PTT

custom parts:
  LM567: Tone detector
